// Logisim project AR.circ as structural Verilog
module AR_Cont (
  input  D4,
  input  D5,
  input  T0,
  input  T2,
  input  T3,
  input  T4,
  output AR_BUS,
  output AR_INC,
  output AR_LD
);

  wire and_1_out, and_2_out;

  and and_1 (and_1_out, T3, D4);
  and and_2 (and_2_out, T4, D5);
  and and_3 (AR_INC, T3, D5);
  or or_1 (AR_LD, T2, T0);
  or or_2 (AR_BUS, and_1_out, and_2_out);
endmodule
