// Logisim project DR.circ as structural Verilog: 2 circuits, main circuit main
module main (
);

  DR_Cont dr_cont_1 ();  // open: D0, D1, D2, T3, T4, DR_BUS, DR_INC, DR_LD
endmodule

module DR_Cont (
  input  D0,
  input  D1,
  input  D2,
  input  T3,
  input  T4,
  output DR_BUS,
  output DR_INC,
  output DR_LD
);

  wire and_1_out, and_2_out, and_3_out, and_4_out, and_5_out, and_6_out;

  and and_1 (and_1_out, T4, D2);
  and and_2 (and_2_out, T4, D0);
  and and_3 (and_3_out, D1, T4);
  and and_4 (and_4_out, T3, D0);
  and and_5 (and_5_out, T3, D1);
  and and_6 (and_6_out, T3, D2);
  or or_1 (DR_BUS, and_1_out, and_2_out, and_3_out);
  or or_2 (DR_LD, and_4_out, and_5_out, and_6_out);
endmodule
