// Logisim project Gunfer.circ as structural Verilog: 12 circuits, main circuit main
module main (
  input  [3:0] Input,
  input  LD,
  input  INC,
  input  CLR,
  output [3:0] Output
);

  wire clock_1_out;

  Clock clock_1 (.out(clock_1_out));
  _4_REG u_4_reg_1 (.INPUT(Input), .CLK(clock_1_out), .LD(LD), .INC(INC), .CLR(CLR), .OUTPUT(Output));
endmodule

// reg.
module _4_REG (
  input  INC,
  input  LD,
  input  [3:0] INPUT,
  input  CLK,
  input  CLR,
  output [3:0] OUTPUT
);

  wire and_1_out, and_2_out, and_3_out, and_4_out, and_5_out, and_6_out, and_7_out, and_8_out, and_9_out,
       and_10_out, and_11_out, and_12_out, not_1_out, not_2_out, not_3_out, not_4_out, not_5_out, not_6_out,
       or_1_out, or_2_out, or_3_out, or_4_out, or_5_out, or_6_out, or_7_out, or_8_out;

  not not_1 (not_1_out, LD);
  not not_2 (not_2_out, not_1_out);
  not not_3 (not_3_out, INPUT[0]);
  not not_4 (not_4_out, INPUT[1]);
  not not_5 (not_5_out, INPUT[2]);
  not not_6 (not_6_out, INPUT[3]);
  and and_1 (and_1_out, INC, not_1_out);
  and and_2 (and_2_out, not_2_out, INPUT[0]);
  and and_3 (and_3_out, not_2_out, not_3_out);
  and and_4 (and_4_out, not_2_out, INPUT[1]);
  and and_5 (and_5_out, not_2_out, not_4_out);
  and and_6 (and_6_out, not_2_out, INPUT[2]);
  and and_7 (and_7_out, not_2_out, not_5_out);
  and and_8 (and_8_out, not_2_out, INPUT[3]);
  and and_9 (and_9_out, not_2_out, not_6_out);
  and and_10 (and_10_out, and_1_out, OUTPUT[0]);
  and and_11 (and_11_out, and_1_out, OUTPUT[0], OUTPUT[1]);
  and and_12 (and_12_out, and_1_out, OUTPUT[0], OUTPUT[1], OUTPUT[2]);
  or or_1 (or_1_out, and_2_out, and_1_out);
  or or_2 (or_2_out, and_3_out, and_1_out);
  or or_3 (or_3_out, and_4_out, and_10_out);
  or or_4 (or_4_out, and_10_out, and_5_out);
  or or_5 (or_5_out, and_6_out, and_11_out);
  or or_6 (or_6_out, and_11_out, and_7_out);
  or or_7 (or_7_out, and_8_out, and_12_out);
  or or_8 (or_8_out, and_12_out, and_9_out);
  J_K_Flip_Flop j_k_ff_1 (.J(or_1_out), .clk(CLK), .K(or_2_out), .Q(OUTPUT[0]), .reset(CLR));  // open: Qn, preset, en
  J_K_Flip_Flop j_k_ff_2 (.J(or_3_out), .clk(CLK), .K(or_4_out), .Q(OUTPUT[1]), .reset(CLR));  // open: Qn, preset, en
  J_K_Flip_Flop j_k_ff_3 (.J(or_5_out), .clk(CLK), .K(or_6_out), .Q(OUTPUT[2]), .reset(CLR));  // open: Qn, preset, en
  J_K_Flip_Flop j_k_ff_4 (.J(or_7_out), .clk(CLK), .K(or_8_out), .Q(OUTPUT[3]), .reset(CLR));  // open: Qn, preset, en
endmodule

module denemeee (
  input  in_1,
  input  in_2
);

  wire clock_1_out, \paket_lab_ödev_1_r1 , \paket_lab_ödev_1_r2 , \paket_lab_ödev_1_r3 ;
  wire [3:0] controlled_buffer_1_out, n4_reg_1_output, n4_reg_2_output, n4_reg_3_output;

  \paket_lab_ödev  \paket_lab_ödev_1  (
    .in_1(in_1), .in_2(in_2), .r1(\paket_lab_ödev_1_r1 ), .r2(\paket_lab_ödev_1_r2 ),
    .r3(\paket_lab_ödev_1_r3 ));
  Clock clock_1 (.out(clock_1_out));
  // Probe on controlled_buffer_1_out
  // Probe on n4_reg_1_output
  _4_REG u_4_reg_1 (
    .INPUT(controlled_buffer_1_out), .CLK(clock_1_out), .LD(\paket_lab_ödev_1_r1 ), .OUTPUT(n4_reg_1_output));  // open: INC, CLR
  // Probe on n4_reg_2_output
  _4_REG u_4_reg_2 (
    .INPUT(controlled_buffer_1_out), .CLK(clock_1_out), .LD(\paket_lab_ödev_1_r2 ), .OUTPUT(n4_reg_2_output));  // open: INC, CLR
  // Probe on n4_reg_3_output
  _4_REG u_4_reg_3 (
    .INPUT(controlled_buffer_1_out), .CLK(clock_1_out), .LD(\paket_lab_ödev_1_r3 ), .OUTPUT(n4_reg_3_output));  // open: INC, CLR
  assign controlled_buffer_1_out = \paket_lab_ödev_1_r3  ? n4_reg_1_output : 4'bz;  // Controlled_Buffer controlled_buffer_1
  assign controlled_buffer_1_out = \paket_lab_ödev_1_r1  ? n4_reg_2_output : 4'bz;  // Controlled_Buffer controlled_buffer_2
  assign controlled_buffer_1_out = \paket_lab_ödev_1_r2  ? n4_reg_3_output : 4'bz;  // Controlled_Buffer controlled_buffer_3
endmodule

module \paket_lab_ödev  (
  input  in_1,
  input  in_2,
  output r1,
  output r2,
  output r3
);

  wire not_1_out, not_2_out;

  not not_1 (not_1_out, in_2);
  not not_2 (not_2_out, in_1);
  nor nor_1 (r1, in_1, in_2);
  nor nor_2 (r2, in_1, not_1_out);
  nor nor_3 (r3, not_2_out, in_2);
endmodule

module ALU_1bit (
  input  AC,
  input  DR,
  input  INPR,
  input  AND,
  input  ADD,
  input  \CİN ,
  input  LD_DR,
  input  CMA,
  input  CIR,
  input  in_10,
  input  CIL,
  input  in_12,
  input  LD_INPR,
  output out_14,
  output OUTPUT
);

  wire ADD_out, adder_1_out, and_1_out, AND_2_out, CMA_out, LD_DR_out, LD_INP_out, not_1_out, SHL_out,
       SHR_out;

  not not_1 (not_1_out, AC);
  and and_1 (and_1_out, DR, AC);
  Adder #(.width(1)) adder_1 (.a(DR), .b(AC), .out(adder_1_out), .cin(\CİN ), .cout(out_14));
  and AND_2 (AND_2_out, AND, and_1_out);
  and u_ADD (ADD_out, ADD, adder_1_out);
  and u_LD_DR (LD_DR_out, LD_DR, DR);
  and u_CMA (CMA_out, CMA, not_1_out);
  and SHR (SHR_out, CIR, in_10);
  and SHL (SHL_out, CIL, in_12);
  and LD_INP (LD_INP_out, LD_INPR, INPR);
  or or_1 (OUTPUT, AND_2_out, ADD_out, LD_DR_out, CMA_out, SHR_out, SHL_out, LD_INP_out);
endmodule

// ALU
module _4bit_alu (
  input  cin,
  input  [3:0] AC,
  input  E_AC_0,
  input  [3:0] DR,
  input  [3:0] INPR,
  input  AND,
  input  ADD,
  input  CMA,
  input  LD_DR,
  input  LD_INPR,
  input  CIR,
  input  CIL,
  input  E_AC3,
  output [3:0] out_14,
  output out_15
);

  wire alu_1bit_1_out_14, alu_1bit_2_out_14, alu_1bit_3_out_14;

  ALU_1bit alu_1bit_1 (
    .AND(AND), .ADD(ADD), .LD_DR(CMA), .CMA(LD_DR), .CIR(LD_INPR), .in_10(CIR), .CIL(CIL), .in_12(E_AC_0),
    .LD_INPR(AC[1]), .AC(INPR[0]), .DR(DR[0]), .INPR(AC[0]), .\CİN (cin), .out_14(alu_1bit_1_out_14),
    .OUTPUT(out_14[0]));
  ALU_1bit alu_1bit_2 (
    .AND(AND), .ADD(ADD), .LD_DR(CMA), .CMA(LD_DR), .CIR(LD_INPR), .in_10(CIR), .CIL(CIL), .in_12(AC[0]),
    .LD_INPR(AC[2]), .AC(INPR[1]), .DR(DR[1]), .INPR(AC[1]), .\CİN (alu_1bit_1_out_14),
    .out_14(alu_1bit_2_out_14), .OUTPUT(out_14[1]));
  ALU_1bit alu_1bit_3 (
    .AND(AND), .ADD(ADD), .LD_DR(CMA), .CMA(LD_DR), .CIR(LD_INPR), .in_10(CIR), .CIL(CIL), .in_12(AC[1]),
    .LD_INPR(AC[3]), .AC(INPR[2]), .DR(DR[2]), .INPR(AC[2]), .\CİN (alu_1bit_2_out_14),
    .out_14(alu_1bit_3_out_14), .OUTPUT(out_14[2]));
  ALU_1bit alu_1bit_4 (
    .AND(AND), .ADD(ADD), .LD_DR(CMA), .CMA(LD_DR), .CIR(LD_INPR), .in_10(CIR), .CIL(CIL), .in_12(AC[2]),
    .LD_INPR(E_AC3), .AC(INPR[3]), .DR(DR[3]), .INPR(AC[3]), .\CİN (alu_1bit_3_out_14), .out_14(out_15),
    .OUTPUT(out_14[3]));
endmodule

module PC_Control (
  input  T0,
  input  T1,
  input  T3,
  input  T4,
  input  D4,
  input  D5,
  input  D6,
  output out_8,
  output out_9,
  output out_10
);

  wire and_1_out, and_2_out, and_3_out, or_1_out;

  or or_1 (or_1_out, D6, D4);
  and and_1 (and_1_out, or_1_out, T3);
  and and_2 (and_2_out, D5, T4);
  and and_3 (and_3_out, D5, T3);
  or or_2 (out_8, and_1_out, and_2_out);
  or or_3 (out_10, and_3_out, T0);

  assign out_9 = T1;
endmodule

module AR (
  input  D4,
  input  D5,
  input  T0,
  input  T2,
  input  T3,
  input  T4,
  output AR_BUS,
  output AR_INC,
  output AR_LD
);

  wire and_1_out, and_2_out;

  and and_1 (and_1_out, D4, T3);
  and and_2 (and_2_out, T4, D5);
  and and_3 (AR_INC, T2, D5);
  or or_1 (AR_LD, T0, T2);
  or or_2 (AR_BUS, and_1_out, and_2_out);
endmodule

module DR (
  input  D0,
  input  D1,
  input  D2,
  input  T3,
  input  T4,
  output DR_BUS,
  output DR_LD
);

  wire and_1_out, and_2_out, and_3_out, and_4_out, and_5_out, and_6_out;

  and and_1 (and_1_out, T4, D2);
  and and_2 (and_2_out, T4, D0);
  and and_3 (and_3_out, D1, T4);
  and and_4 (and_4_out, D0, T3);
  and and_5 (and_5_out, T3, D1);
  and and_6 (and_6_out, T3, D2);
  or or_1 (DR_BUS, and_1_out, and_2_out, and_3_out);
  or or_2 (DR_LD, and_4_out, and_5_out, and_6_out);
endmodule

module IR (
  input  T1,
  input  T2,
  output IR_BUS,
  output IR_LD
);


  assign IR_BUS = T2;
  assign IR_LD = T1;
endmodule

module Project (
  input  [3:0] INPR
);

  wire clock_1_out;
  wire [3:0] AC_output, AR_output, controlled_buffer_1_out, controlled_buffer_1_out_2, DR_output,
       n4bit_alu_1_out_14, OUTR_output, PC_output;
  wire [7:0] IR_out_6, ram_1_data;

  _4bit_alu u_4bit_alu_1 (
    .AC(AC_output), .DR(DR_output), .INPR(INPR), .out_14(n4bit_alu_1_out_14));  // open: AND, ADD, CMA, LD_DR, LD_INPR, CIR, CIL, cin, E_AC_0, out_15, E_AC3
  Clock clock_1 (.out(clock_1_out));
  RAM #(.addrWidth(4), .bus("separate")) ram_1 (
    .addr(AR_output), .din({controlled_buffer_1_out_2, controlled_buffer_1_out}), .data(ram_1_data),
    .clk(clock_1_out));  // open: str, sel, ld, clr
  _4_REG AR (.INPUT(controlled_buffer_1_out), .CLK(clock_1_out), .OUTPUT(AR_output));  // open: LD, INC, CLR
  // Probe on PC_output
  _4_REG PC (.INPUT(controlled_buffer_1_out), .CLK(clock_1_out), .OUTPUT(PC_output));  // open: LD, INC, CLR
  // Probe on DR_output
  _4_REG DR (.INPUT(controlled_buffer_1_out), .CLK(clock_1_out), .OUTPUT(DR_output));  // open: LD, INC, CLR
  // Probe on AC_output
  _4_REG AC (.INPUT(n4bit_alu_1_out_14), .CLK(clock_1_out), .OUTPUT(AC_output));  // open: LD, INC, CLR
  // Probe on IR_out_6
  _8_reg IR (
    .in_1({controlled_buffer_1_out_2, controlled_buffer_1_out}), .CLOCk(clock_1_out), .out_6(IR_out_6));  // open: LOAD, INC, CLR
  // Probe on OUTR_output
  _4_REG OUTR (.INPUT(controlled_buffer_1_out), .CLK(clock_1_out), .OUTPUT(OUTR_output));  // open: LD, INC, CLR
  // Probe on AR_output
  // Probe on OUTR_output
  Controlled_Buffer #(.width(8)) controlled_buffer_1 (
    .in({4'b0000, AR_output}), .out({controlled_buffer_1_out_2, controlled_buffer_1_out}));  // open: en
  Controlled_Buffer #(.width(8)) controlled_buffer_2 (
    .in({4'b0000, PC_output}), .out({controlled_buffer_1_out_2, controlled_buffer_1_out}));  // open: en
  Controlled_Buffer #(.width(8)) controlled_buffer_3 (
    .in({4'b0000, DR_output}), .out({controlled_buffer_1_out_2, controlled_buffer_1_out}));  // open: en
  Controlled_Buffer #(.width(8)) controlled_buffer_4 (
    .in({4'b0000, AC_output}), .out({controlled_buffer_1_out_2, controlled_buffer_1_out}));  // open: en
  Controlled_Buffer #(.width(8)) controlled_buffer_5 (
    .in(IR_out_6), .out({controlled_buffer_1_out_2, controlled_buffer_1_out}));  // open: en
  // Probe on {controlled_buffer_1_out_2, controlled_buffer_1_out}
  Controlled_Buffer #(.width(8)) controlled_buffer_6 (
    .in(ram_1_data), .out({controlled_buffer_1_out_2, controlled_buffer_1_out}));  // open: en
endmodule

module _8_reg (
  input  [7:0] in_1,
  input  CLOCk,
  input  LOAD,
  input  CLR,
  input  INC,
  output [7:0] out_6
);

  _4_REG u_4_reg_1 (.INPUT(in_1[3:0]), .CLK(CLOCk), .LD(LOAD), .INC(INC), .CLR(CLR), .OUTPUT(out_6[3:0]));
  _4_REG u_4_reg_2 (.INPUT(in_1[7:4]), .CLK(CLOCk), .LD(LOAD), .INC(INC), .CLR(CLR), .OUTPUT(out_6[7:4]));
endmodule
