// Logisim project IR.circ as structural Verilog
module IR_Cont (
  input  T1,
  input  T2,
  output IR_BUS,
  output IR_LD
);


  assign IR_BUS = T2;
  assign IR_LD = T1;
endmodule
