// Logisim project Lab_1.circ as structural Verilog: 5 circuits, main circuit S1_F1
module S1_F1 (
  input  A,
  input  B,
  input  C,
  output out_4
);

  wire AB__prime_out, AC_out, B_prime_C_out, not_1_out, not_2_out;

  not not_1 (not_1_out, B);
  and AB__prime (AB__prime_out, A, B);
  not not_2 (not_2_out, AB__prime_out);
  and AC (AC_out, A, C);
  and B_prime_C (B_prime_C_out, not_1_out, C);
  or F1 (out_4, not_2_out, AC_out, B_prime_C_out);

  // Notes on the sheet:
  //   F1 = (AB)’ + AC + B’C
endmodule

module S1_F2 (
  input  A,
  input  B,
  input  C,
  output out_4
);

  wire A_prime_BC_out, AB_prime___BA_prime_out, AB_prime_out, ABC_prime___A_prime_BC__prime_out,
       ABC_prime_out, BA_prime_out, not_1_out, not_2_out, not_3_out, not_4_out;

  not not_1 (not_1_out, C);
  not not_2 (not_2_out, A);
  not not_3 (not_3_out, B);
  not not_4 (not_4_out, A);
  and ABC_prime (ABC_prime_out, not_1_out, B, A);
  and A_prime_BC (A_prime_BC_out, C, B, not_2_out);
  and AB_prime (AB_prime_out, not_3_out, A);
  and BA_prime (BA_prime_out, B, not_4_out);
  nor ABC_prime___A_prime_BC__prime (ABC_prime___A_prime_BC__prime_out, ABC_prime_out, A_prime_BC_out);
  or AB_prime___BA_prime (AB_prime___BA_prime_out, AB_prime_out, BA_prime_out);
  and F2 (out_4, ABC_prime___A_prime_BC__prime_out, AB_prime___BA_prime_out);

  // Notes on the sheet:
  //   F2 = (ABC’ + A’BC)’ . (AB’ + BA’)
endmodule

module S1_F3 (
  input  A,
  input  B,
  input  C,
  output out_4
);

  wire A_BC__prime___AB_prime_C_prime_out, A_prime___B_out, A_prime_B__B_BC_prime_out, B___BC_prime_out,
       BC_prime_out, not_1_out, not_2_out, not_3_out, not_4_out;

  and BC_prime (BC_prime_out, B, not_1_out);
  not not_1 (not_1_out, C);
  not not_2 (not_2_out, C);
  not not_3 (not_3_out, B);
  not not_4 (not_4_out, A);
  and A_BC__prime___AB_prime_C_prime (A_BC__prime___AB_prime_C_prime_out, not_2_out, not_3_out, A);
  or A_prime___B (A_prime___B_out, B, not_4_out);
  or B___BC_prime (B___BC_prime_out, B, BC_prime_out);
  and A_prime_B__B_BC_prime (A_prime_B__B_BC_prime_out, A_prime___B_out, B___BC_prime_out);
  or F3 (out_4, A_prime_B__B_BC_prime_out, A_BC__prime___AB_prime_C_prime_out);

  // Notes on the sheet:
  //   F3 = (A’ + B) (B + BC’) + A (BC)’
endmodule

module S2_F1 (
  input  A,
  input  B,
  input  C,
  output out_4
);

  wire and_1_out, and_2_out, nand_1_out, not_1_out, or_1_out;

  not not_1 (not_1_out, A);
  nand nand_1 (nand_1_out, B, A);
  or or_1 (or_1_out, nand_1_out, C);
  and and_1 (and_1_out, not_1_out, C);
  and and_2 (and_2_out, not_1_out, or_1_out);
  xor F1 (out_4, and_1_out, and_2_out);
endmodule

module S2_F2 (
  input  A,
  input  B,
  input  C,
  output out_4
);

  wire and_1_out, and_2_out, and_3_out, and_4_out, nand_1_out, not_1_out, or_1_out, xor_1_out;

  not not_1 (not_1_out, A);
  nand nand_1 (nand_1_out, C, B);
  or or_1 (or_1_out, nand_1_out, A);
  and and_1 (and_1_out, nand_1_out, C);
  and and_2 (and_2_out, C, B);
  and and_3 (and_3_out, not_1_out, B);
  and and_4 (and_4_out, not_1_out, or_1_out);
  xor xor_1 (xor_1_out, and_1_out, and_2_out);
  or F2 (out_4, and_3_out, and_4_out, xor_1_out);
endmodule
