// Logisim project Lab_2.circ as structural Verilog: 3 circuits, main circuit main
module main (
  input  CLK,
  output Q3,
  output Q2,
  output Q1,
  output Q0
);

  wire clock_1_out, nand_1_out;

  S1_A s1_a_1 (.CLK(nand_1_out), .Q1(Q3), .Q0(Q2));
  Clock clock_1 (.out(clock_1_out));
  S1_A s1_a_2 (.CLK(clock_1_out), .Q1(Q1), .Q0(Q0));
  nand nand_1 (nand_1_out, Q0, Q1);
endmodule

// 2 Bit
module S1_A (
  input  CLK,
  output Q1,
  output Q0
);

  J_K_Flip_Flop j_k_ff_1 (.J(Q0), .clk(CLK), .K(Q0), .Q(Q1));  // open: Qn, preset, en, reset
  J_K_Flip_Flop j_k_ff_2 (.J(1'b1), .clk(CLK), .K(1'b1), .Q(Q0));  // open: Qn, preset, en, reset
endmodule

module _8_16_Bits_Counter (
  output [7:0] \_8_Bitlik_Sayıcı ,
  output [15:0] \_16_Bitlik_Sayıcı 
);

  wire clock_1_out, clock_2_out, nand_1_out, nand_2_out, nand_3_out, nand_4_out, nand_5_out, nand_6_out,
       nand_7_out, nand_8_out, nand_9_out, nand_10_out;

  S1_A s1_a_1 (.CLK(nand_1_out), .Q1(\_8_Bitlik_Sayıcı [7]), .Q0(\_8_Bitlik_Sayıcı [6]));
  S1_A s1_a_2 (.CLK(nand_3_out), .Q1(\_8_Bitlik_Sayıcı [5]), .Q0(\_8_Bitlik_Sayıcı [4]));
  S1_A s1_a_3 (.CLK(nand_4_out), .Q1(\_16_Bitlik_Sayıcı [13]), .Q0(\_16_Bitlik_Sayıcı [12]));
  S1_A s1_a_4 (.CLK(nand_2_out), .Q1(\_16_Bitlik_Sayıcı [15]), .Q0(\_16_Bitlik_Sayıcı [14]));
  nand nand_1 (nand_1_out, \_8_Bitlik_Sayıcı [5], \_8_Bitlik_Sayıcı [4]);
  nand nand_2 (nand_2_out, \_16_Bitlik_Sayıcı [13], \_16_Bitlik_Sayıcı [12]);
  S1_A s1_a_5 (.CLK(nand_5_out), .Q1(\_8_Bitlik_Sayıcı [3]), .Q0(\_8_Bitlik_Sayıcı [2]));
  nand nand_3 (nand_3_out, \_8_Bitlik_Sayıcı [3], \_8_Bitlik_Sayıcı [2]);
  Clock clock_1 (.out(clock_1_out));
  S1_A s1_a_6 (.CLK(nand_6_out), .Q1(\_16_Bitlik_Sayıcı [11]), .Q0(\_16_Bitlik_Sayıcı [10]));
  nand nand_4 (nand_4_out, \_16_Bitlik_Sayıcı [11], \_16_Bitlik_Sayıcı [10]);
  S1_A s1_a_7 (.CLK(clock_1_out), .Q1(\_8_Bitlik_Sayıcı [1]), .Q0(\_8_Bitlik_Sayıcı [0]));
  nand nand_5 (nand_5_out, \_8_Bitlik_Sayıcı [1], \_8_Bitlik_Sayıcı [0]);
  S1_A s1_a_8 (.CLK(nand_7_out), .Q1(\_16_Bitlik_Sayıcı [9]), .Q0(\_16_Bitlik_Sayıcı [8]));
  nand nand_6 (nand_6_out, \_16_Bitlik_Sayıcı [9], \_16_Bitlik_Sayıcı [8]);
  S1_A s1_a_9 (.CLK(nand_8_out), .Q1(\_16_Bitlik_Sayıcı [7]), .Q0(\_16_Bitlik_Sayıcı [6]));
  nand nand_7 (nand_7_out, \_16_Bitlik_Sayıcı [7], \_16_Bitlik_Sayıcı [6]);
  S1_A s1_a_10 (.CLK(nand_9_out), .Q1(\_16_Bitlik_Sayıcı [5]), .Q0(\_16_Bitlik_Sayıcı [4]));
  nand nand_8 (nand_8_out, \_16_Bitlik_Sayıcı [5], \_16_Bitlik_Sayıcı [4]);
  S1_A s1_a_11 (.CLK(nand_10_out), .Q1(\_16_Bitlik_Sayıcı [3]), .Q0(\_16_Bitlik_Sayıcı [2]));
  S1_A s1_a_12 (.CLK(clock_2_out), .Q1(\_16_Bitlik_Sayıcı [1]), .Q0(\_16_Bitlik_Sayıcı [0]));
  nand nand_9 (nand_9_out, \_16_Bitlik_Sayıcı [3], \_16_Bitlik_Sayıcı [2]);
  Clock clock_2 (.out(clock_2_out));
  nand nand_10 (nand_10_out, \_16_Bitlik_Sayıcı [1], \_16_Bitlik_Sayıcı [0]);
endmodule
