// Logisim project Lab_4.circ as structural Verilog: 2 circuits, main circuit main
module main (
  input  [3:0] in_1,
  input  INC,
  input  CLR,
  input  LD,
  input  in_5,
  input  in_6,
  input  in_7,
  input  in_8,
  input  INC_2,
  input  CLR_2,
  input  LD_2,
  input  in_12,
  input  in_13,
  input  C1,
  input  C2,
  input  INC_3,
  input  CLR_3,
  input  LD_3,
  input  in_19,
  input  C1_2,
  input  C2_2,
  input  C1_3,
  input  C2_3,
  output Q1,
  output Q2,
  output Q3,
  output Q1_2,
  output Q2_2,
  output Q3_2,
  output Q1_3,
  output Q2_3,
  output Q3_3,
  output Q1_4,
  output Q2_4,
  output Q3_4
);

  wire clock_1_out, comparator_1_eq, comparator_1_gt, comparator_2_eq, comparator_2_gt, comparator_3_eq,
       comparator_3_gt, s2_1_q1, s2_1_q2, s2_1_q3;
  wire [3:0] R1_p2, R1_p7, R2_p7, R3_p7;

  S2 s2_1 (.C1(in_6), .C2(in_7), .Q1(s2_1_q1), .Q2(s2_1_q2), .Q3(s2_1_q3));
  S2 s2_2 (.C1(in_8), .C2(in_13), .Q1(Q1), .Q2(Q2), .Q3(Q3));
  Comparator #(.width(1), .mode("unsigned")) comparator_1 (
    .a(C1), .b(C2), .gt(comparator_1_gt), .eq(comparator_1_eq));  // open: lt
  Comparator #(.width(1), .mode("unsigned")) comparator_2 (
    .a(C1_2), .b(C2_2), .gt(comparator_2_gt), .eq(comparator_2_eq));  // open: lt
  Comparator #(.width(1), .mode("unsigned")) comparator_3 (
    .a(C1_3), .b(C2_3), .gt(comparator_3_gt), .eq(comparator_3_eq));  // open: lt
  Comparator #(.width(1), .mode("unsigned")) comparator_4 (
    .a(comparator_1_eq), .b(comparator_1_gt), .gt(Q1_2), .eq(Q2_2), .lt(Q3_2));
  Comparator #(.width(1), .mode("unsigned")) comparator_5 (
    .a(comparator_2_eq), .b(comparator_2_gt), .gt(Q1_3), .eq(Q2_3), .lt(Q3_3));
  Comparator #(.width(1), .mode("unsigned")) comparator_6 (
    .a(comparator_3_eq), .b(comparator_3_gt), .gt(Q1_4), .eq(Q2_4), .lt(Q3_4));
  Clock clock_1 (.out(clock_1_out));
  // Probe on R1_p7
  // _4_reg R1: pin names not known; wires that end beside it: LD, R1_p2, clock_1_out, s2_1_q1, INC, CLR, R1_p7
  // Probe on R2_p7
  // _4_reg R2: pin names not known; wires that end beside it: LD_2, R1_p2, clock_1_out, s2_1_q2, INC_2, CLR_2, R2_p7
  // Probe on R3_p7
  // _4_reg R3: pin names not known; wires that end beside it: LD_3, R1_p2, clock_1_out, s2_1_q3, INC_3, CLR_3, R3_p7
  assign R1_p2 = s2_1_q3 ? R1_p7 : 4'bz;  // Controlled_Buffer controlled_buffer_1
  assign R1_p2 = s2_1_q1 ? R2_p7 : 4'bz;  // Controlled_Buffer controlled_buffer_2
  assign R1_p2 = s2_1_q2 ? R3_p7 : 4'bz;  // Controlled_Buffer controlled_buffer_3
  // Probe on R1_p2
endmodule

module S2 (
  input  C1,
  input  C2,
  output Q1,
  output Q2,
  output Q3
);

  wire comparator_1_eq, comparator_1_gt;

  Comparator #(.width(1), .mode("unsigned")) comparator_1 (
    .a(C1), .b(C2), .gt(comparator_1_gt), .eq(comparator_1_eq));  // open: lt
  Comparator #(.width(1), .mode("unsigned")) comparator_2 (
    .a(comparator_1_eq), .b(comparator_1_gt), .gt(Q1), .eq(Q2), .lt(Q3));
endmodule
