// Logisim project PC.circ as structural Verilog: 2 circuits, main circuit main
module main (
);

  wire controlled_buffer_1_out, n4_reg_1_p2;

  Controlled_Buffer controlled_buffer_1 (.in(n4_reg_1_p2), .out(controlled_buffer_1_out));  // open: en
  // _4_reg 4_reg_1: pin names not known; wires that end beside it: controlled_buffer_1_out, n4_reg_1_p2
endmodule

module PC_Cont (
  input  D4,
  input  D5,
  input  D6,
  input  T0,
  input  T1,
  input  T3,
  input  T4,
  output PC_BUS,
  output PC_INC,
  output PC_LD
);

  wire and_1_out, and_2_out, and_3_out, and_4_out;

  and and_1 (and_1_out, D5, T3);
  and and_2 (and_2_out, D4, T3);
  and and_3 (and_3_out, D5, T4);
  and and_4 (and_4_out, D6, T3);
  or or_1 (PC_BUS, T0, and_1_out);
  or or_2 (PC_LD, and_2_out, and_3_out, and_4_out);

  assign PC_INC = T1;
endmodule
