// Logisim project Taslak.circ as structural Verilog: 3 circuits, main circuit main
module main (
);

  _4Reg INPR ();  // open: in_3, CLK, LD, INC, CLR, out_6
  _8Reg IR ();  // open: in_1, in_2, CLK, LD, INC, CLR
  RAM #(.addrWidth(4), .bus("separate")) ram_1 ();  // open: addr, din, data, str, sel, clk, ld, clr
  _4Reg AR ();  // open: in_3, CLK, LD, INC, CLR, out_6
  _4Reg PC ();  // open: in_3, CLK, LD, INC, CLR, out_6
  _4Reg DR ();  // open: in_3, CLK, LD, INC, CLR, out_6
  _4Reg AC ();  // open: in_3, CLK, LD, INC, CLR, out_6
  _4Reg OUTR ();  // open: in_3, CLK, LD, INC, CLR, out_6
endmodule

module _4Reg (
  input  INC,
  input  LD,
  input  [3:0] in_3,
  input  CLK,
  input  CLR,
  output [3:0] out_6
);

  wire and_1_out, and_2_out, and_3_out, and_4_out, and_5_out, and_6_out, and_7_out, and_8_out, and_9_out,
       and_10_out, and_11_out, and_12_out, not_1_out, not_2_out, not_3_out, not_4_out, not_5_out, not_6_out,
       or_1_out, or_2_out, or_3_out, or_4_out, or_5_out, or_6_out, or_7_out, or_8_out;

  not not_1 (not_1_out, LD);
  and and_1 (and_1_out, INC, not_1_out);
  not not_2 (not_2_out, not_1_out);
  not not_3 (not_3_out, in_3[0]);
  not not_4 (not_4_out, in_3[1]);
  not not_5 (not_5_out, in_3[2]);
  not not_6 (not_6_out, in_3[3]);
  and and_2 (and_2_out, not_2_out, in_3[0]);
  and and_3 (and_3_out, not_2_out, not_3_out);
  and and_4 (and_4_out, not_2_out, in_3[1]);
  and and_5 (and_5_out, not_2_out, not_4_out);
  and and_6 (and_6_out, not_2_out, in_3[2]);
  and and_7 (and_7_out, not_2_out, not_5_out);
  and and_8 (and_8_out, not_2_out, in_3[3]);
  and and_9 (and_9_out, not_2_out, not_6_out);
  and and_10 (and_10_out, and_1_out, out_6[0]);
  and and_11 (and_11_out, and_1_out, out_6[0], out_6[1]);
  and and_12 (and_12_out, and_1_out, out_6[0], out_6[1], out_6[2]);
  or or_1 (or_1_out, and_2_out, and_1_out);
  or or_2 (or_2_out, and_3_out, and_1_out);
  or or_3 (or_3_out, and_4_out, and_10_out);
  or or_4 (or_4_out, and_10_out, and_5_out);
  or or_5 (or_5_out, and_6_out, and_11_out);
  or or_6 (or_6_out, and_11_out, and_7_out);
  or or_7 (or_7_out, and_8_out, and_12_out);
  or or_8 (or_8_out, and_12_out, and_9_out);
  J_K_Flip_Flop j_k_ff_1 (.J(or_1_out), .clk(CLK), .K(or_2_out), .Q(out_6[0]), .reset(CLR));  // open: Qn, preset, en
  J_K_Flip_Flop j_k_ff_2 (.J(or_3_out), .clk(CLK), .K(or_4_out), .Q(out_6[1]), .reset(CLR));  // open: Qn, preset, en
  J_K_Flip_Flop j_k_ff_3 (.J(or_5_out), .clk(CLK), .K(or_6_out), .Q(out_6[2]), .reset(CLR));  // open: Qn, preset, en
  J_K_Flip_Flop j_k_ff_4 (.J(or_7_out), .clk(CLK), .K(or_8_out), .Q(out_6[3]), .reset(CLR));  // open: Qn, preset, en
endmodule

module _8Reg (
  input  [7:0] in_1,
  input  [7:0] in_2,
  input  LD,
  input  CLR,
  input  INC,
  input  CLK
);

  wire [3:0] n4reg_1_out_6, n4reg_2_out_6;

  _4Reg u_4reg_1 (.in_3(in_2[3:0]), .CLK(CLK), .LD(LD), .INC(INC), .CLR(CLR), .out_6(n4reg_1_out_6));
  _4Reg u_4reg_2 (.in_3(in_2[7:4]), .CLK(CLK), .LD(LD), .INC(INC), .CLR(CLR), .out_6(n4reg_2_out_6));
endmodule
